# Fritzing sketch Jarvis_Arduino (saved by Fritzing 0.9.3b)
breadboards: 1

parts:
  Part1 = Arduino Uno (Rev3)
  Q1 = LTR-301 [package=ltr-301]
  R1 = Resistor [tolerance=±5% resistance=10k package=THT]
  U1 = TMP36 [package=to-92]

nets:
  N1: Part1.A0, U1.VOUT
  N2: Part1.A1, Q1.E, R1.Pin_1
  5V: Part1.5V, Q1.C, U1.VCC
  GND: Part1.GND, R1.Pin_0, U1.GND
