# Fritzing sketch Jarvis_RPi (saved by Fritzing 0.9.3b)
breadboards: 5

parts:
  R1 = Resistor [tolerance=±5% resistance=220 package=THT]
  M1 = DC Motor
  LED1 = LED - 3mm [color="Green (555nm)" package="3 mm [THT]"]
  LED2 = LED - 3mm [color="Green (555nm)" package="3 mm [THT]"]
  LED3 = LED - 3mm [color="Green (555nm)" package="3 mm [THT]"]
  LED4 = LED - 3mm [color="Green (555nm)" package="3 mm [THT]"]
  LED5 = LED - 3mm [color="Green (555nm)" package="3 mm [THT]"]
  R2 = Resistor [tolerance=±5% resistance=220 package=THT]
  R3 = Resistor [tolerance=±5% resistance=220 package=THT]
  R4 = Resistor [tolerance=±5% resistance=220 package=THT]
  R5 = Resistor [tolerance=±5% resistance=220 package=THT]
  R6 = Resistor [tolerance=±5% resistance=220 package=THT]
  LED6 = LED - 3mm [color="Yellow (585nm)" package="3 mm [THT]"]
  LED7 = LED - 3mm [color="Yellow (585nm)" package="3 mm [THT]"]
  LED8 = LED - 3mm [color="Yellow (585nm)" package="3 mm [THT]"]
  U1 = LCD-16X2 [package=lcd-16x2_noholes]
  Raspberry_Pi_1 = Raspberry Pi 3 [part_number=RPI-3-V1.2]
  IC1 = L293D [package=THT]

nets:
  VDD: R1.Pin_0, U1.VDD, Raspberry_Pi_1.5V, IC1.+Vmotor, IC1.+V
  N1: R1.Pin_1, U1.A
  N2: M1.pin_1, IC1.Out_1_(_Controlled_by_Enable_1_)
  N3: M1.pin_2, IC1.Out_2_(_Controlled_by_Enable_1_)
  VSS: LED1.cathode, LED2.cathode, LED3.cathode, LED4.cathode, LED5.cathode, LED6.cathode, LED7.cathode, LED8.cathode, U1.VSS, U1.RS, U1.K, Raspberry_Pi_1.GND, IC1.0V
  N4: LED1.anode, R2.Pin_0
  N5: LED2.anode, R5.Pin_0
  N6: LED3.anode, R6.Pin_0
  N7: LED4.anode, R3.Pin_0
  N8: LED5.anode, R4.Pin_0
  N9: R2.Pin_1, Raspberry_Pi_1.GIPO4
  N10: R3.Pin_1, Raspberry_Pi_1.GIPO17
  N11: R4.Pin_1, Raspberry_Pi_1.GIPO10, Raspberry_Pi_1.GIPO9
  3V3: R5.Pin_1, Raspberry_Pi_1.3v3, Raspberry_Pi_1.GIPO22, Raspberry_Pi_1.3V3
  N12: R6.Pin_1, Raspberry_Pi_1.GIPO27
  N13: LED6.anode, LED7.anode, LED8.anode, Raspberry_Pi_1.GIPO26
  N14: U1.VO, Raspberry_Pi_1.ID_SC, Raspberry_Pi_1.GIPO7
  N15: U1.R_W, Raspberry_Pi_1.GIPO8
  N16: U1.DB4, Raspberry_Pi_1.GIPO25
  N17: U1.DB5, Raspberry_Pi_1.GIPO24
  N18: U1.DB6, Raspberry_Pi_1.GIPO23
  N19: U1.DB7, Raspberry_Pi_1.GIPO18
  N20: Raspberry_Pi_1.GIPO21, IC1.In_2
  N21: Raspberry_Pi_1.GIPO20, IC1.In_1
  N22: Raspberry_Pi_1.GIPO16, IC1.Enable_1
